# Fritzing sketch analogSwitchCircuit (saved by Fritzing 0.9.3b)
circuit board: 8.82076cm x 3.77284cm
stripboards: 1

parts:
  S10 = Pushbutton [package="[SMD]"]
  S11 = Pushbutton [package="[SMD]"]
  S12 = Pushbutton [package="[SMD]"]
  S13 = Pushbutton [package="[SMD]"]
  R4 = Resistor [tolerance=±5% resistance=1M package=THT]
  R3 = Resistor [tolerance=±5% resistance=470k package=THT]
  R2 = Resistor [tolerance=±5% resistance=100k package=THT]
  R1 = Resistor [tolerance=±5% resistance=47k package=THT]
  R5 = Resistor [tolerance=±5% resistance=10k package=THT]
  J2 = female pin header, 1 pin [form="♀ (female)"]

nets:
  N1: S10.Pin_1, S10.Pin_2, S11.Pin_1, S11.Pin_2, S12.Pin_1, S12.Pin_2, S13.Pin_1, S13.Pin_2, R5.Pin_0, J2.pin1
  N2: S10.Pin_3, S10.Pin_4, R4.Pin_1
  N3: S11.Pin_3, S11.Pin_4, R3.Pin_1
  N4: S12.Pin_3, S12.Pin_4, R2.Pin_0
  N5: S13.Pin_3, S13.Pin_4, R1.Pin_0
  5V: R4.Pin_0, R3.Pin_0, R2.Pin_1, R1.Pin_1
  GND: R5.Pin_1
